// Logisim project PR_2_carno.circ as structural Verilog: 3 circuits, main circuit main
module main (
  output out_1,
  output out_2
);

  wire and_1_out, and_2_out, and_3_out, clock_1_out, counter_1_carry, t_ff_1_q,
       \мднф_по_карте_карно_1_out_6 , \мднф_по_куайна_мак_класски_1_out_6 ;
  wire [4:0] counter_1_q;
  wire [31:0] shift_register_1_q0, shift_register_2_q0;

  and and_1 (and_1_out, clock_1_out, ~counter_1_carry);  // AND_Gate
  Clock clock_1 (.out(clock_1_out));
  Counter #(.width(5), .max('h1f)) counter_1 (
    .Q(counter_1_q), .carry(counter_1_carry), .clk(and_1_out));  // open: load, D, count, clr
  and and_2 (and_2_out, ~t_ff_1_q, counter_1_carry);  // AND_Gate
  T_Flip_Flop t_ff_1 (.clk(clock_1_out), .T(and_2_out), .Q(t_ff_1_q));  // open: Qn, preset, reset, en
  and and_3 (and_3_out, clock_1_out, ~t_ff_1_q);  // AND_Gate
  \МДНФ_по_Куайна_Мак_Класски  \u_мднф_по_куайна_мак_класски_1  (
    .out_6(\мднф_по_куайна_мак_класски_1_out_6 ), .in_1(counter_1_q[4]), .in_2(counter_1_q[3]),
    .in_3(counter_1_q[2]), .in_4(counter_1_q[1]), .in_5(counter_1_q[0]));
  \МДНФ_по_карте_карно  \u_мднф_по_карте_карно_1  (
    .out_6(\мднф_по_карте_карно_1_out_6 ), .in_1(counter_1_q[4]), .in_2(counter_1_q[3]),
    .in_3(counter_1_q[2]), .in_4(counter_1_q[1]), .in_5(counter_1_q[0]));
  Shift_Register #(.length(32)) shift_register_1 (
    .in(\мднф_по_куайна_мак_класски_1_out_6 ), .clk(and_3_out), .q0(shift_register_1_q0[0]),
    .q1(shift_register_1_q0[1]), .q2(shift_register_1_q0[2]), .q3(shift_register_1_q0[3]),
    .q4(shift_register_1_q0[4]), .q5(shift_register_1_q0[5]), .q6(shift_register_1_q0[6]),
    .q7(shift_register_1_q0[7]), .q8(shift_register_1_q0[8]), .q9(shift_register_1_q0[9]),
    .q10(shift_register_1_q0[10]), .q11(shift_register_1_q0[11]), .q12(shift_register_1_q0[12]),
    .q13(shift_register_1_q0[13]), .q14(shift_register_1_q0[14]), .q15(shift_register_1_q0[15]),
    .q16(shift_register_1_q0[16]), .q17(shift_register_1_q0[17]), .q18(shift_register_1_q0[18]),
    .q19(shift_register_1_q0[19]), .q20(shift_register_1_q0[20]), .q21(shift_register_1_q0[21]),
    .q22(shift_register_1_q0[22]), .q23(shift_register_1_q0[23]), .q24(shift_register_1_q0[24]),
    .q25(shift_register_1_q0[25]), .q26(shift_register_1_q0[26]), .q27(shift_register_1_q0[27]),
    .q28(shift_register_1_q0[28]), .q29(shift_register_1_q0[29]), .q30(shift_register_1_q0[30]),
    .q31(shift_register_1_q0[31]));  // open: shift, out, load, clr, d0, d1, d2, d3, d4, d5, d6, d7, d8, d9, d10, d11, d12, d13, d14, d15, d16, d17, d18, d19, d20, d21, d22, d23, d24, d25, d26, d27, d28, d29, d30, d31
  Shift_Register #(.length(32)) shift_register_2 (
    .in(\мднф_по_карте_карно_1_out_6 ), .clk(and_3_out), .q0(shift_register_2_q0[0]),
    .q1(shift_register_2_q0[1]), .q2(shift_register_2_q0[2]), .q3(shift_register_2_q0[3]),
    .q4(shift_register_2_q0[4]), .q5(shift_register_2_q0[5]), .q6(shift_register_2_q0[6]),
    .q7(shift_register_2_q0[7]), .q8(shift_register_2_q0[8]), .q9(shift_register_2_q0[9]),
    .q10(shift_register_2_q0[10]), .q11(shift_register_2_q0[11]), .q12(shift_register_2_q0[12]),
    .q13(shift_register_2_q0[13]), .q14(shift_register_2_q0[14]), .q15(shift_register_2_q0[15]),
    .q16(shift_register_2_q0[16]), .q17(shift_register_2_q0[17]), .q18(shift_register_2_q0[18]),
    .q19(shift_register_2_q0[19]), .q20(shift_register_2_q0[20]), .q21(shift_register_2_q0[21]),
    .q22(shift_register_2_q0[22]), .q23(shift_register_2_q0[23]), .q24(shift_register_2_q0[24]),
    .q25(shift_register_2_q0[25]), .q26(shift_register_2_q0[26]), .q27(shift_register_2_q0[27]),
    .q28(shift_register_2_q0[28]), .q29(shift_register_2_q0[29]), .q30(shift_register_2_q0[30]),
    .q31(shift_register_2_q0[31]));  // open: shift, out, load, clr, d0, d1, d2, d3, d4, d5, d6, d7, d8, d9, d10, d11, d12, d13, d14, d15, d16, d17, d18, d19, d20, d21, d22, d23, d24, d25, d26, d27, d28, d29, d30, d31
  Comparator #(.width(32)) comparator_1 (.a(shift_register_1_q0), .b(32'h478e9c16), .eq(out_1));  // open: gt, lt
  Comparator #(.width(32)) comparator_2 (.a(shift_register_2_q0), .b(32'h478e9c16), .eq(out_2));  // open: gt, lt

  // Notes on the sheet:
  //   f = 478E9C16
endmodule

module \МДНФ_по_Куайна_Мак_Класски  (
  input  in_1,
  input  in_2,
  input  in_3,
  input  in_4,
  input  in_5,
  output out_6
);

  wire and_1_out, and_2_out, and_3_out, and_4_out, and_5_out, and_6_out, and_7_out;

  and and_1 (and_1_out, ~in_1, ~in_2, ~in_4, in_5);  // AND_Gate
  and and_2 (and_2_out, ~in_1, in_2, ~in_4, ~in_5);  // AND_Gate
  and and_3 (and_3_out, in_1, ~in_2, ~in_4, ~in_5);  // AND_Gate
  and and_4 (and_4_out, in_2, in_3, in_4, ~in_5);  // AND_Gate
  and and_5 (and_5_out, in_1, ~in_3, in_4, in_5);  // AND_Gate
  and and_6 (and_6_out, ~in_1, ~in_2, in_3, in_4);  // AND_Gate
  and and_7 (and_7_out, in_3, ~in_4, in_5);  // AND_Gate
  or or_1 (out_6, and_1_out, and_2_out, and_3_out, and_4_out, and_5_out, and_6_out, and_7_out);
endmodule

module \МДНФ_по_карте_карно  (
  input  in_1,
  input  in_2,
  input  in_3,
  input  in_4,
  input  in_5,
  output out_6
);

  wire and_1_out, and_2_out, and_3_out, and_4_out, and_5_out, and_6_out, and_7_out;

  and and_1 (and_1_out, ~in_1, ~in_2, ~in_4, in_5);  // AND_Gate
  and and_2 (and_2_out, ~in_1, in_2, ~in_4, ~in_5);  // AND_Gate
  and and_3 (and_3_out, in_1, ~in_2, ~in_4, ~in_5);  // AND_Gate
  and and_4 (and_4_out, in_2, in_3, in_4, ~in_5);  // AND_Gate
  and and_5 (and_5_out, in_1, ~in_3, in_4, in_5);  // AND_Gate
  and and_6 (and_6_out, ~in_1, ~in_2, in_3, in_4);  // AND_Gate
  and and_7 (and_7_out, in_3, ~in_4, in_5);  // AND_Gate
  or or_1 (out_6, and_1_out, and_2_out, and_3_out, and_4_out, and_5_out, and_6_out, and_7_out);
endmodule
