// Logisim project PR_2_mux.circ as structural Verilog: 1 circuit, main circuit main
module main (
  input  x4,
  input  x3,
  input  x2,
  input  x1,
  input  x0,
  output out_6
);

  wire multiplexer_1_out, multiplexer_2_out, multiplexer_3_out, multiplexer_4_out, multiplexer_5_out,
       multiplexer_6_out, multiplexer_7_out, multiplexer_8_out, multiplexer_9_out, multiplexer_10_out,
       multiplexer_11_out, multiplexer_12_out, multiplexer_13_out, multiplexer_14_out, not_1_out, not_2_out,
       not_3_out, not_4_out;

  not not_1 (not_1_out, x0);
  not not_2 (not_2_out, x0);
  not not_3 (not_3_out, x0);
  not not_4 (not_4_out, x0);
  Multiplexer multiplexer_1 (.in0(x0), .in1(1'b0), .out(multiplexer_1_out), .sel(x1));  // open: en
  Multiplexer multiplexer_2 (.in0(x0), .in1(1'b1), .out(multiplexer_2_out), .sel(x1));  // open: en
  Multiplexer multiplexer_3 (.in0(not_1_out), .in1(1'b0), .out(multiplexer_3_out), .sel(x1));  // open: en
  Multiplexer multiplexer_4 (.in0(1'b1), .in1(not_2_out), .out(multiplexer_4_out), .sel(x1));  // open: en
  Multiplexer multiplexer_5 (.in0(not_3_out), .in1(x0), .out(multiplexer_5_out), .sel(x1));  // open: en
  Multiplexer multiplexer_6 (.in0(1'b1), .in1(1'b0), .out(multiplexer_6_out), .sel(x1));  // open: en
  Multiplexer multiplexer_7 (.in0(1'b0), .in1(x0), .out(multiplexer_7_out), .sel(x1));  // open: en
  Multiplexer multiplexer_8 (.in0(x0), .in1(not_4_out), .out(multiplexer_8_out), .sel(x1));  // open: en
  Multiplexer #(.enable("false")) multiplexer_9 (
    .in0(multiplexer_1_out), .in1(multiplexer_2_out), .out(multiplexer_9_out), .sel(x2));
  Multiplexer #(.enable("false")) multiplexer_10 (
    .in0(multiplexer_3_out), .in1(multiplexer_4_out), .out(multiplexer_10_out), .sel(x2));
  Multiplexer #(.enable("false")) multiplexer_11 (
    .in0(multiplexer_5_out), .in1(multiplexer_6_out), .out(multiplexer_11_out), .sel(x2));
  Multiplexer #(.enable("false")) multiplexer_12 (
    .in0(multiplexer_7_out), .in1(multiplexer_8_out), .out(multiplexer_12_out), .sel(x2));
  Multiplexer #(.enable("false")) multiplexer_13 (
    .in0(multiplexer_9_out), .in1(multiplexer_10_out), .out(multiplexer_13_out), .sel(x3));
  Multiplexer #(.enable("false")) multiplexer_14 (
    .in0(multiplexer_11_out), .in1(multiplexer_12_out), .out(multiplexer_14_out), .sel(x3));
  Multiplexer #(.enable("false")) multiplexer_15 (
    .in0(multiplexer_13_out), .in1(multiplexer_14_out), .out(out_6), .sel(x4));
endmodule
