// Logisim project PR_2_1_2.circ as structural Verilog: 1 circuit, main circuit main
module main (
  input  in_1,
  output out_2
);

  wire clock_1_out, rom_2_data;
  wire [2:0] register_1_q, rom_1_data;

  Clock clock_1 (.out(clock_1_out));
  ROM #(.addrWidth(4), .dataWidth(3)) rom_1 (.addr({register_1_q, in_1}), .data(rom_1_data));  // open: sel
  Register #(.width(3)) register_1 (.D(rom_1_data), .Q(register_1_q), .clk(clock_1_out));  // open: en, clr
  ROM #(.addrWidth(4), .dataWidth(1)) rom_2 (.addr({register_1_q, in_1}), .data(rom_2_data));  // open: sel
  D_Flip_Flop d_ff_1 (.clk(clock_1_out), .D(rom_2_data), .Q(out_2));  // open: Qn, preset, en, reset

  // Notes on the sheet:
  //   contents of rom_1 (hex, n*v repeats v):
  //   3 1 2 1 3 1 3 4 3 1
  //   contents of rom_2 (hex, n*v repeats v):
  //   0 1 1 1 0 1 0 0 0 1
endmodule
