// Logisim project PR_2_3.circ as structural Verilog: 2 circuits, main circuit main
module main (
  input  in_1,
  input  in_2,
  input  in_3,
  input  in_4,
  output out_5
);

  wire clock_1_out, min_1_y, min_2_y, min_3_y, min_4_y;

  Clock clock_1 (.out(clock_1_out));
  MIN min_1 (.m(out_5), .d(in_1), .clk(clock_1_out), .y(min_1_y));
  MIN min_2 (.m(out_5), .d(in_2), .clk(clock_1_out), .y(min_2_y));
  MIN min_3 (.m(out_5), .d(in_3), .clk(clock_1_out), .y(min_3_y));
  MIN min_4 (.m(out_5), .d(in_4), .clk(clock_1_out), .y(min_4_y));
  and and_1 (out_5, min_1_y, min_2_y, min_3_y, min_4_y);
endmodule

module MIN (
  input  m,
  input  d,
  input  clk,
  output y
);

  wire and_1_out, d_ff_1_q, or_1_out;

  and and_1 (and_1_out, ~m, d);  // AND_Gate
  or or_1 (or_1_out, and_1_out, d_ff_1_q);
  D_Flip_Flop d_ff_1 (.clk(clk), .D(or_1_out), .Q(d_ff_1_q));  // open: Qn, preset, en, reset
  or or_2 (y, d, d_ff_1_q);
endmodule
