// Logisim project Pr_2_2_3.circ as structural Verilog: 4 circuits, main circuit main
module main (
  input  in_1,
  input  in_2,
  output out_3
);

  wire clock_1_out, local_sfm_1_out, local_sfm_2_out, or_1_out;

  Clock clock_1 (.out(clock_1_out));
  local_sfm local_sfm_1 (.CLK(clock_1_out), .OUT(local_sfm_1_out), .IN1(in_1), .IN2(in_2));
  local_sfm local_sfm_2 (.CLK(clock_1_out), .OUT(local_sfm_2_out), .IN1(in_2), .IN2(in_1));
  or or_1 (or_1_out, local_sfm_1_out, local_sfm_2_out);
  chet_nechet chet_nechet_1 (.in_1(or_1_out), .in_2(clock_1_out), .out_3(out_3));
endmodule

module local_sfm (
  input  IN1,
  input  IN2,
  input  CLK,
  output OUT
);

  wire rom_2_data;
  wire [2:0] rom_1_data;
  wire [4:2] register_1_q;

  Register #(.width(3)) register_1 (.D(rom_1_data), .Q(register_1_q), .clk(CLK));  // open: en, clr
  ROM #(.addrWidth(5), .dataWidth(3)) rom_1 (.addr({register_1_q, IN1, IN2}), .data(rom_1_data));  // open: sel
  ROM #(.addrWidth(5), .dataWidth(1)) rom_2 (.addr({register_1_q, IN1, IN2}), .data(rom_2_data));  // open: sel
  D_Flip_Flop d_ff_1 (.clk(CLK), .D(rom_2_data), .Q(OUT));  // open: Qn, preset, en, reset

  // Notes on the sheet:
  //   contents of rom_1 (hex, n*v repeats v):
  //   0 1 2 0 0 1 2 3 0 1 2 4 0 1 2 3 0 1 2 4
  //   contents of rom_2 (hex, n*v repeats v):
  //   9*0 1 4*0 1 0 0 1
endmodule

module chet_nechet (
  input  in_1,
  input  in_2,
  output out_3
);

  wire rom_1_data;
  wire [1:1] register_1_q;

  ROM #(.addrWidth(2), .dataWidth(1)) rom_1 (.addr({register_1_q[1], in_1}), .data(rom_1_data));  // open: sel
  Register #(.width(1)) register_1 (.D(rom_1_data), .Q(register_1_q[1]), .clk(in_2));  // open: en, clr
  ROM #(.addrWidth(2), .dataWidth(1)) rom_2 (.addr({register_1_q[1], in_1}), .data(out_3));  // open: sel

  // Notes on the sheet:
  //   contents of rom_1 (hex, n*v repeats v):
  //   0 1 1
  //   contents of rom_2 (hex, n*v repeats v):
  //   0 1 1
endmodule

module chet_nechet_2 (
  input  in_1,
  input  in_2,
  output out_3
);

  wire rom_1_data;

  ROM #(.addrWidth(2), .dataWidth(1)) rom_1 (.addr({out_3, in_1}), .data(rom_1_data));  // open: sel
  Register #(.width(1)) register_1 (.D(rom_1_data), .Q(out_3), .clk(in_2));  // open: en, clr

  // Notes on the sheet:
  //   contents of rom_1 (hex, n*v repeats v):
  //   0 1 1
endmodule
