// Logisim project counter_on_jk_trigger_example.circ as structural Verilog: 1 circuit, main circuit main
module main (
  output out_1,
  output out_2,
  output out_3,
  output out_4,
  output out_5
);

  wire clock_1_out, nor_1_out, nor_2_out, nor_3_out, nor_4_out, nor_5_out, nor_6_out, nor_7_out, nor_8_out,
       nor_9_out;

  nor nor_1 (nor_1_out, ~out_4, ~out_5);  // NOR_Gate
  nor nor_2 (nor_2_out, out_1, out_1);
  nor nor_3 (nor_3_out, ~out_1, ~out_5);  // NOR_Gate
  nor nor_4 (nor_4_out, ~out_5, ~out_3, ~out_2);  // NOR_Gate
  nor nor_5 (nor_5_out, out_2, ~out_3);  // NOR_Gate
  nor nor_6 (nor_6_out, out_3, ~out_4);  // NOR_Gate
  nor nor_7 (nor_7_out, out_1, out_4);
  nor nor_8 (nor_8_out, nor_5_out, nor_6_out, nor_7_out);
  nor nor_9 (nor_9_out, ~out_2, ~out_3, nor_1_out);  // NOR_Gate
  Clock clock_1 (.out(clock_1_out));
  J_K_Flip_Flop j_k_ff_1 (.J(nor_9_out), .clk(clock_1_out), .K(1'b1), .Q(out_1));  // open: Qn, preset, en, reset
  J_K_Flip_Flop j_k_ff_2 (.J(out_3), .clk(clock_1_out), .K(out_3), .Q(out_2));  // open: Qn, preset, en, reset
  J_K_Flip_Flop j_k_ff_3 (.J(nor_2_out), .clk(clock_1_out), .K(1'b1), .Q(out_3));  // open: Qn, preset, en, reset
  J_K_Flip_Flop j_k_ff_4 (.J(nor_3_out), .clk(clock_1_out), .K(nor_4_out), .Q(out_4));  // open: Qn, preset, en, reset
  J_K_Flip_Flop j_k_ff_5 (.J(out_1), .clk(clock_1_out), .K(nor_8_out), .Q(out_5));  // open: Qn, preset, en, reset
  Hex_Digit_Display hex_digit_display_1 (.value({out_2, out_3, out_4, out_5}));  // open: dp

  // Other names for the same wires on the sheet: Q0 = out_5; Q1 = out_4; Q2 = out_3; Q3 = out_2; Q4 = out_1

  // Notes on the sheet:
  //   S4
  //   S3
  //   S2
  //   S1
  //   S0
endmodule
