// Logisim project example_3.circ as structural Verilog: 2 circuits, main circuit main
module main (
  input  in_1,
  input  in_2,
  input  in_3,
  output out_4
);

  wire clock_1_out, local_fsm_1_y, local_fsm_2_y, local_fsm_3_y;

  Clock clock_1 (.out(clock_1_out));
  local_fsm local_fsm_1 (.m(out_4), .d(in_1), .clk(clock_1_out), .y(local_fsm_1_y));
  local_fsm local_fsm_2 (.m(out_4), .d(in_2), .clk(clock_1_out), .y(local_fsm_2_y));
  local_fsm local_fsm_3 (.m(out_4), .d(in_3), .clk(clock_1_out), .y(local_fsm_3_y));
  or or_1 (out_4, local_fsm_1_y, local_fsm_2_y, local_fsm_3_y);

  // Notes on the sheet:
  //   Вывод максимального из трех чисел
endmodule

module local_fsm (
  input  m,
  input  d,
  input  clk,
  output y
);

  wire and_1_out, d_ff_1_q, or_1_out;

  and and_1 (and_1_out, m, ~d);  // AND_Gate
  or or_1 (or_1_out, and_1_out, d_ff_1_q);
  D_Flip_Flop d_ff_1 (.clk(clk), .D(or_1_out), .Q(d_ff_1_q));  // open: Qn, preset, en, reset
  and and_2 (y, d, ~d_ff_1_q);  // AND_Gate
endmodule
