// Logisim project example_4.circ as structural Verilog: 1 circuit, main circuit main
module main (
  input  IN
);

  wire CLK;
  wire [0:0] counter_1_q;
  wire [1:0] register_1_q, rom_1_data;

  Clock clock_1 (.out(CLK));
  Counter #(.width(1), .max('h1)) counter_1 (.Q(counter_1_q[0]), .clk(CLK));  // open: load, D, count, carry, clr
  ROM #(.addrWidth(4), .dataWidth(2)) rom_1 (
    .addr({register_1_q, IN, counter_1_q[0]}), .data(rom_1_data));  // open: sel
  Register #(.width(2)) register_1 (.D(rom_1_data), .Q(register_1_q), .clk(CLK));  // open: en, clr
  Hex_Digit_Display hex_digit_display_1 (.value({2'b00, register_1_q}));  // open: dp

  // Notes on the sheet:
  //   Свертка по mod 3
  //   contents of rom_1 (hex, n*v repeats v):
  //   0 0 1 2 1 1 2 0 2 2 0 1
endmodule
