// Logisim project example_4645645645645.circ as structural Verilog: 1 circuit, main circuit main
module main (
  input  IN
);

  wire CLK;
  wire [1:0] undriven;
  wire [2:0] counter_1_q, register_1_q, rom_1_data;

  Counter #(.width(3), .max('h6)) counter_1 (.Q(counter_1_q), .clk(CLK));  // open: load, D, count, carry, clr
  Clock clock_1 (.out(CLK));
  ROM #(.addrWidth(6), .dataWidth(3)) rom_1 (.addr({register_1_q, IN, undriven}), .data(rom_1_data));  // open: sel
  Register #(.width(3)) register_1 (.D(rom_1_data), .Q(register_1_q), .clk(CLK));  // open: en, clr
  Hex_Digit_Display hex_digit_display_1 (.value({1'b0, register_1_q}));  // open: dp

  // Notes on the sheet:
  //   Свертка по mod 3
  //   contents of rom_1 (hex, n*v repeats v):
  //   0 0 0 1 2 3 4 5 6 1 1 1 2 3 4 5 6 0 2 2 2 3 4 5 6 0 1 3 3 3 4 5 6 0 1 2 4 4 4 5 6 0 1 2 3 5 5 5 6 0
  //   1 2 3 4 6 6 6 0 1 2 3 4 5
endmodule
