// Logisim project Финальная_версия_2_задания_теория_автоматов.circ as structural Verilog: 4 circuits, main circuit main
module main (
  input  in_1,
  input  in_2,
  output out_3,
  output out_4
);

  wire clock_1_out, iscl_1_out, norm_scheme_1_out, xor_1_out;

  Clock clock_1 (.out(clock_1_out));
  norm_scheme norm_scheme_1 (.OUT(norm_scheme_1_out), .IN1(in_1), .IN2(in_2), .CLK(clock_1_out));
  iscl iscl_1 (.OUT(iscl_1_out), .IN1(in_2), .IN2(in_1), .CLK(clock_1_out));
  and and_1 (out_4, norm_scheme_1_out, iscl_1_out);
  xor xor_1 (xor_1_out, out_3, out_4);
  D_Flip_Flop d_ff_1 (.clk(clock_1_out), .D(xor_1_out), .Q(out_3));  // open: Qn, preset, en, reset
endmodule

module local_sfm (
  input  IN1,
  input  IN2,
  input  CLK,
  output OUT
);

  wire rom_2_data;
  wire [1:0] rom_1_data;
  wire [3:2] register_1_q;

  ROM #(.addrWidth(4), .dataWidth(2)) rom_1 (.addr({register_1_q, IN1, IN2}), .data(rom_1_data));  // open: sel
  Register #(.width(2)) register_1 (.D(rom_1_data), .Q(register_1_q), .clk(CLK));  // open: en, clr
  ROM #(.addrWidth(4), .dataWidth(1)) rom_2 (.addr({register_1_q, IN1, IN2}), .data(rom_2_data));  // open: sel
  D_Flip_Flop d_ff_1 (.clk(CLK), .D(rom_2_data), .Q(OUT));  // open: Qn, preset, en, reset

  // Notes on the sheet:
  //   contents of rom_1 (hex, n*v repeats v):
  //   1 0 2 0 1 0 2 3 1 0 2 3 1 0 2 3
  //   contents of rom_2 (hex, n*v repeats v):
  //   12*0 1 0 1
endmodule

module norm_scheme (
  input  IN1,
  input  IN2,
  input  CLK,
  output OUT
);

  wire rom_2_data;
  wire [2:0] rom_1_data;
  wire [4:2] register_1_q;

  ROM #(.addrWidth(5), .dataWidth(3)) rom_1 (.addr({register_1_q, IN1, IN2}), .data(rom_1_data));  // open: sel
  Register #(.width(3)) register_1 (.D(rom_1_data), .Q(register_1_q), .clk(CLK));  // open: en, clr
  ROM #(.addrWidth(5), .dataWidth(1)) rom_2 (.addr({register_1_q, IN1, IN2}), .data(rom_2_data));  // open: sel
  D_Flip_Flop d_ff_1 (.clk(CLK), .D(rom_2_data), .Q(OUT));  // open: Qn, preset, en, reset

  // Notes on the sheet:
  //   contents of rom_1 (hex, n*v repeats v):
  //   1 0 2 3 1 0 2 4 1 0 2 5 1 0 2 3 1 0 2 4 1 0 2 5
  //   contents of rom_2 (hex, n*v repeats v):
  //   12*0 1 0 1 0 1 0 1 0 1 0 1
endmodule

module iscl (
  input  IN1,
  input  IN2,
  input  CLK,
  output OUT
);

  wire rom_2_data;
  wire [1:0] rom_1_data;
  wire [3:2] register_1_q;

  Register #(.width(2)) register_1 (.D(rom_1_data), .Q(register_1_q), .clk(CLK));  // open: en, clr
  ROM #(.addrWidth(4), .dataWidth(2)) rom_1 (.addr({register_1_q, IN1, IN2}), .data(rom_1_data));  // open: sel
  ROM #(.addrWidth(4), .dataWidth(1)) rom_2 (.addr({register_1_q, IN1, IN2}), .data(rom_2_data));  // open: sel
  D_Flip_Flop d_ff_1 (.clk(CLK), .D(rom_2_data), .Q(OUT));  // open: Qn, preset, en, reset

  // Notes on the sheet:
  //   contents of rom_1 (hex, n*v repeats v):
  //   0 1 0 0 0 1 0 2 0 1 0 2
  //   contents of rom_2 (hex, n*v repeats v):
  //   7*1 0 1 1 0 5*1
endmodule
